# Fritzing sketch Capstone Project (saved by Fritzing 1.0.1rc)
breadboards: 1

parts:
  DS2 = DS18B20 1-Wire Temperature Sensor Probe
  S10 = PH meter [package=THT]
  LCD2 = 20x4 LCD display [part_number=2004A]
  LCM1602_IIC2 = LCM1602 IIC [part_number="LCM1602 IIC" chip_label="LCM1602 IIC" package="DIP (Dual Inline) [THT]"]
  Part5 = Arduino Nano (Rev3.0) (ICSP)
  WeMos_D1_R1 = WeMos D1 R2
  U5 = GAS_SENSOR [package=mq-3]
  R1 = Resistor [tolerance=±5% resistance=220 package="2010 [SMD]"]
  Mod3 = KY-019 5V Relay Module [package="Breakout board"]

nets:
  GND: DS2.GND, Part5.GND
  N1: DS2.VDD, Part5.A0, R1.Pin_1
  N2: S10.pin1, Part5.A2
  N3: S10.pin2, LCM1602_IIC2.VCC, U5.B1, Mod3.+
  N4: S10.pin3, LCM1602_IIC2.GND, U5.A1, Mod3.-
  VSS: LCD2.Vss, LCM1602_IIC2.VSS
  VDD: LCD2.Vdd, LCM1602_IIC2.VDD
  N5: LCD2.Vo, LCM1602_IIC2.V0
  N6: LCD2.RS, LCM1602_IIC2.RS
  N7: LCD2.R/W, LCM1602_IIC2.RW
  N8: LCD2.E, LCM1602_IIC2.E
  N9: LCD2.DB0, LCM1602_IIC2.D0
  N10: LCD2.DB1, LCM1602_IIC2.D1
  N11: LCD2.DB2, LCM1602_IIC2.D2
  N12: LCD2.DB3, LCM1602_IIC2.D3
  N13: LCD2.DB4, LCM1602_IIC2.D4
  N14: LCD2.DB5, LCM1602_IIC2.D5
  N15: LCD2.DB6, LCM1602_IIC2.D6
  N16: LCD2.DB7, LCM1602_IIC2.D7
  N17: LCD2.A_+, LCM1602_IIC2.A
  N18: LCD2.K_-, LCM1602_IIC2.K
  N19: LCM1602_IIC2.SDA, Part5.A4
  N20: LCM1602_IIC2.SCL, Part5.A5
  N21: LCM1602_IIC2.LED_A, LCM1602_IIC2.LED_B
  N22: Part5.D1/TX, WeMos_D1_R1.D0/RX
  N23: Part5.D0/RX, WeMos_D1_R1.D1/TX
  N24: Part5.5V, R1.Pin_0
  N25: Part5.A1, U5.H1
  N26: WeMos_D1_R1.(D5), Mod3.S

custom parts:
  20x4 LCD display: 20x4 character display. CHECK LED POLARITY BEFORE CONNECTING POWER Some versions of the dispaly have the polarity of the LED pins "A" and "K" reversed.
  LCM1602 IIC: I2C-Module to use a 1602 or 2004 LCD on with the wire.h libory Serial LCD Modul
  WeMos D1 R2: The D1 R2 is a mini wifi board based on the ESP-8266EX.
  KY-019 5V Relay Module: KY-019 5V Relay module, used to control AC circuits. (Special thanks to vanepp for fixing the PCB holes and other errors)

// code stored in the sketch: nano_pale.ino
#include <Wire.h>
#include <LiquidCrystal_I2C.h>

LiquidCrystal_I2C lcd(0x27, 20, 4);

const int ntcPin    = A0;
const int mq135Pin  = A1;
const int phPin     = A2;

float temperature, ammonia, phValue;
unsigned long previousMillis = 0;
const long interval = 5000; // interval pembacaan sensor setiap 5 detik

void setup() {
  Serial.begin(115200);
  lcd.begin();
  lcd.backlight();
}

void loop() {
  unsigned long currentMillis = millis();

  // Baca nilai sensor setiap 5 detik
  if (currentMillis - previousMillis >= interval) {
    previousMillis = currentMillis;
    
    // Baca nilai sensor
    temperature = bacaSuhu(ntcPin);
    ammonia = bacaAmmonia(mq135Pin);
    phValue = bacaPh(phPin);

    // Kirim data ke NodeMCU melalui Serial
    Serial.print("T");
    Serial.println(temperature);
    Serial.print("A");
    Serial.println(ammonia);
    Serial.print("P");
    Serial.println(phValue);

    // Update tampilan LCD
    updateLCD();
  }
}

float bacaSuhu(int pin) {
  const double referenceResistance = 7107.02; // Nilai resistansi referensi pada suhu 25°C
  const double referenceTemperature = 25.0; // Suhu referensi (°C) untuk resistansi referensi
  const double betaCoefficient = 3950.0; // Koefisien Beta NTC Thermistor
  const double seriesResistor = 10000.0; // Nilai resistor seri pada rangkaian

  // Baca nilai analog dari NTC Thermistor
  int ntcValue = analogRead(pin);

  // Konversi nilai analog menjadi resistansi NTC Thermistor
  double resistance = seriesResistor / (1023.0 / ntcValue - 1.0);

  // Hitung suhu menggunakan persamaan Steinhart-Hart
  double steinhart;
  steinhart = log(resistance / referenceResistance);
  steinhart /= betaCoefficient;
  steinhart += 1.0 / (referenceTemperature + 273.15);
  steinhart = 1.0 / steinhart - 273.15;

  // Kalibrasi suhu jika diperlukan
  double calibratedTemperature = kalibrasiSuhu(steinhart);

  // Tampilkan hasil di Serial Monitor
//  Serial.print("ADC Value: ");
//  Serial.print(ntcValue);
//  Serial.print(", Resistance: ");
//  Serial.print(resistance);
//  Serial.print(" Ohms, Temperature: ");
//  Serial.print(calibratedTemperature);
//  Serial.println(" °C");
  
  return calibratedTemperature;
}

// Fungsi untuk kalibrasi suhu sesuai kebutuhan Anda
double kalibrasiSuhu(double suhuAwal) {
  // Tambahkan logika kalibrasi di sini
  // Contoh: return suhuAwal + offset;
  // Tambahkan logika kalibrasi di sini
  // Contoh: return suhuAwal + offset;
  double offset = 0.0; // Sesuaikan dengan nilai offset yang diperlukan
  return suhuAwal + offset;
}

float bacaAmmonia(int pin) {
  float VRL = analogRead(pin) * (3.3 / 10230);
  float RS = (3.3 / VRL - 1) * 10;
  float Ro = 28; // Ganti dengan nilai RO yang sesuai
  float ratio = RS / Ro;
  float ppm = pow(10, ((log10(ratio) - 0.858) / -0.417));
  return ppm;
}

float bacaPh(int pin) {
  // Baca nilai analog dari sensor pH
  int adcPH = analogRead(pin);

  // Konversi nilai analog menjadi tegangan
  float voltage = adcPH * (5.0 / 1023.0);

  // Konversi tegangan menjadi nilai pH
  // Sesuaikan kemiringan (slope) dan offset sesuai dengan karakteristik sensor Anda
  float pHValue = 7.0 - (voltage - 2.5); // Contoh sederhana, sesuaikan sesuai karakteristik sensor Anda

  // Pastikan nilai pH berada dalam rentang 0-14
  pHValue = constrain(pHValue, 0.0, 14.0);

  return pHValue;
}

void updateLCD() {
  lcd.clear();
  lcd.setCursor(0, 0);
  lcd.print("Pale App - CH2-PS022");

  lcd.setCursor(0, 1);
  lcd.print("Temp    : ");
  lcd.print(temperature);
  lcd.setCursor(15, 1);
  lcd.print(" *C");

  lcd.setCursor(0, 2);
  lcd.print("Ammonia : ");
  lcd.print(ammonia);
  lcd.setCursor(15, 2);
  lcd.print(" mg/L");

  lcd.setCursor(0, 3);
  lcd.print("pH      : ");
  lcd.print(phValue);
  lcd.setCursor(15, 3);
  lcd.print(" pH");
}

// code stored in the sketch: nodemcu_pale.ino
#include <ESP8266WiFi.h>
#include <PubSubClient.h>

WiFiClient espClient;
PubSubClient client(espClient);

// Konfigurasi WiFi
const char *ssid           = "BEJE";
const char *password       = "latiefganteng";

// Konfigurasi MQTT
const char *mqtt_server    = "34.31.59.23";
const int  mqtt_port       = 1883;
const char *mqtt_username  = "pale";
const char *mqtt_password  = "Pale123!";

// Konfigurasi Pin pada LED
const int ledPin    = 14; // GPIO 14 on ESP-12E NodeMCU board

void setup() {
  Serial.begin(115200);
  pinMode(ledPin, OUTPUT); // Set pin LED sebagai output
  client.setCallback(callback);

  // Sambungkan ke WiFi
  connectWiFi();

  // Sambungkan ke MQTT
  connectMQTT();
}

void loop() {
  if (!client.connected()) {
    connectMQTT();
  }
  client.loop();
  
  // Baca data dari Arduino Nano melalui Serial
  while (Serial.available()) {
    char dataType = Serial.read();

    // Map tipe sensor ke topik MQTT
    const char* sensorTypes[3] = {"T", "A", "P"};
    const char* mqttTopics[3] = {"sensor/NTC/tempInC", "sensor/MQ135/ammonia", "sensor/PH/phValue"};

    // Cari indeks tipe sensor
    int sensorIndex = -1;
    for (int i = 0; i < 3; ++i) {
      if (dataType == sensorTypes[i][0]) {
        sensorIndex = i;
        break;
      }
    }

    // Jika indeks valid, simpan nilai sensor dan kirim ke MQTT
    if (sensorIndex >= 0 && sensorIndex < 3) {
      // Baca nilai sensor dari Serial
      float sensorValue = Serial.parseFloat();

      // Debugging (opsional)
      Serial.print("Received ");
      Serial.print(sensorTypes[sensorIndex]);
      Serial.print(": ");
      Serial.println(sensorValue);

      // Kirim nilai sensor ke MQTT
      String topic   = mqttTopics[sensorIndex];
      String payload = String(sensorValue);
      client.publish(topic.c_str(), payload.c_str());
    }
  }

  delay(1000); // Delay untuk stabilitas Serial Communication
}

void connectWiFi() {
  Serial.println("Connecting to WiFi...");
  WiFi.begin(ssid, password);
  while (WiFi.status() != WL_CONNECTED) {
    delay(1000);
    Serial.println("Connecting to WiFi...");
  }
  Serial.println("Connected to WiFi");
}

void connectMQTT() {
  Serial.println("Connecting to MQTT...");
  client.setServer(mqtt_server, mqtt_port);
  while (!client.connected()) {
    if (client.connect("NodeMCU_Client", mqtt_username, mqtt_password)) {
      Serial.println("Connected to MQTT");
      client.subscribe("katup");
    } else {
      delay(1000);
      Serial.println("Connecting to MQTT...");
    }
  }
}

// This functions is executed when some device publishes a message to a topic that your NodeMCU is subscribed to
void callback(char* topic, byte* message, unsigned int length) {
  Serial.print("Message arrived on topic: ");
  Serial.print(topic);
  Serial.print(". Message: ");
  String messageInfo;

  for (int i = 0; i < length; i++) {
    Serial.print((char)message[i]);
    messageInfo += (char)message[i];
  }
  Serial.println();

  // If a message is received on the topic room/lamp, you check if the message is either on or off. Turns the lamp GPIO according to the message
  if(strcmp(topic, "katup") == 0){
      Serial.print("Changing katup to ");
      if(messageInfo == "on"){
        digitalWrite(ledPin, HIGH);
        Serial.print("On");
      }
      else if(messageInfo == "off"){
        digitalWrite(ledPin, LOW);
        Serial.print("Off");
      }
  }
  Serial.println();
}

// code stored in the sketch: nodered_pale.ino
[
    {
        "id": "564e011e075fac28",
        "type": "tab",
        "label": "PALE",
        "disabled": false,
        "info": "",
        "env": []
    },
    {
        "id": "3572d07acf83b089",
        "type": "tab",
        "label": "PALE Backup",
        "disabled": true,
        "info": "",
        "env": []
    },
    {
        "id": "8234be649768a71d",
        "type": "mqtt-broker",
        "name": "PALE Server",
        "broker": "34.31.59.23",
        "port": "1883",
        "clientid": "",
        "autoConnect": true,
        "usetls": false,
        "protocolVersion": "3",
        "keepalive": "60",
        "cleansession": true,
        "autoUnsubscribe": true,
        "birthTopic": "",
        "birthQos": "0",
        "birthPayload": "",
        "birthMsg": {},
        "closeTopic": "",
        "closePayload": "",
        "closeMsg": {},
        "willTopic": "",
        "willQos": "0",
        "willPayload": "",
        "willMsg": {},
        "userProps": "",
        "sessionExpiry": ""
    },
    {
        "id": "dff9603e172e1d75",
        "type": "ui_tab",
        "name": "ESP8266",
        "icon": "dashboard",
        "order": 2,
        "disabled": false,
        "hidden": false
    },
    {
        "id": "1e36cea02d905e42",
        "type": "ui_tab",
        "name": "Katup",
        "icon": "Katup",
        "disabled": false,
        "hidden": false
    },
    {
        "id": "bd16d2bb7a66f39a",
        "type": "ui_group",
        "name": "ESP8266 Thermistor NTC MQTT",
        "tab": "dff9603e172e1d75",
        "order": 1,
        "disp": true,
        "width": "6",
        "collapse": false,
        "className": ""
    },
    {
        "id": "c079f1c984b05fe4",
        "type": "ui_group",
        "name": "MQ135",
        "tab": "dff9603e172e1d75",
        "order": 3,
        "disp": true,
        "width": "6",
        "collapse": false,
        "className": ""
    },
    {
        "id": "7425084c949fae29",
        "type": "ui_group",
        "name": "Sensor Ph",
        "tab": "dff9603e172e1d75",
        "order": 5,
        "disp": true,
        "width": "6",
        "collapse": false,
        "className": ""
    },
    {
        "id": "5d457e5c9d017707",
        "type": "ui_base",
        "theme": {
            "name": "theme-light",
            "lightTheme": {
                "default": "#0094CE",
                "baseColor": "#0094CE",
                "baseFont": "-apple-system,BlinkMacSystemFont,Segoe UI,Roboto,Oxygen-Sans,Ubuntu,Cantarell,Helvetica Neue,sans-serif",
                "edited": true,
                "reset": false
            },
            "darkTheme": {
                "default": "#097479",
                "baseColor": "#097479",
                "baseFont": "-apple-system,BlinkMacSystemFont,Segoe UI,Roboto,Oxygen-Sans,Ubuntu,Cantarell,Helvetica Neue,sans-serif",
                "edited": false
            },
            "customTheme": {
                "name": "Untitled Theme 1",
                "default": "#4B7930",
                "baseColor": "#4B7930",
                "baseFont": "-apple-system,BlinkMacSystemFont,Segoe UI,Roboto,Oxygen-Sans,Ubuntu,Cantarell,Helvetica Neue,sans-serif"
            },
            "themeState": {
                "base-color": {
                    "default": "#0094CE",
                    "value": "#0094CE",
                    "edited": false
                },
                "page-titlebar-backgroundColor": {
                    "value": "#0094CE",
                    "edited": false
                },
                "page-backgroundColor": {
                    "value": "#fafafa",
                    "edited": false
                },
                "page-sidebar-backgroundColor": {
                    "value": "#ffffff",
                    "edited": false
                },
                "group-textColor": {
                    "value": "#1bbfff",
                    "edited": false
                },
                "group-borderColor": {
                    "value": "#ffffff",
                    "edited": false
                },
                "group-backgroundColor": {
                    "value": "#ffffff",
                    "edited": false
                },
                "widget-textColor": {
                    "value": "#111111",
                    "edited": false
                },
                "widget-backgroundColor": {
                    "value": "#0094ce",
                    "edited": false
                },
                "widget-borderColor": {
                    "value": "#ffffff",
                    "edited": false
                },
                "base-font": {
                    "value": "-apple-system,BlinkMacSystemFont,Segoe UI,Roboto,Oxygen-Sans,Ubuntu,Cantarell,Helvetica Neue,sans-serif"
                }
            },
            "angularTheme": {
                "primary": "indigo",
                "accents": "blue",
                "warn": "red",
                "background": "grey",
                "palette": "light"
            }
        },
        "site": {
            "name": "Node-RED Dashboard",
            "hideToolbar": "false",
            "allowSwipe": "false",
            "lockMenu": "false",
            "allowTempTheme": "true",
            "dateFormat": "DD/MM/YYYY",
            "sizes": {
                "sx": 48,
                "sy": 48,
                "gx": 6,
                "gy": 6,
                "cx": 6,
                "cy": 6,
                "px": 0,
                "py": 0
            }
        }
    },
    {
        "id": "372add3cda52af51",
        "type": "MySQLdatabase",
        "name": "DATABASE PALE",
        "host": "34.31.59.23",
        "port": "3306",
        "db": "pale_db",
        "tz": "",
        "charset": "UTF8"
    },
    {
        "id": "071e31b8c3ba162e",
        "type": "ui_group",
        "name": "Katup",
        "tab": "1e36cea02d905e42",
        "order": 4,
        "disp": true,
        "width": "6",
        "collapse": false,
        "className": ""
    },
    {
        "id": "c123303c31dd9f0f",
        "type": "comment",
        "z": "564e011e075fac28",
        "name": "WARNING: please check you have started this container with a volume that is mounted to /data\\n otherwise any flow changes are lost when you redeploy or upgrade the container\\n (e.g. upgrade to a more recent node-red docker image).\\n  If you are using named volumes you can ignore this warning.\\n Double click or see info side panel to learn how to start Node-RED in Docker to save your work",
        "info": "\nTo start docker with a bind mount volume (-v option), for example:\n\n```\ndocker run -it -p 1880:1880 -v /home/user/node_red_data:/data --name mynodered nodered/node-red\n```\n\nwhere `/home/user/node_red_data` is a directory on your host machine where you want to store your flows.\n\nIf you do not do this then you can experiment and redploy flows, but if you restart or upgrade the container the flows will be disconnected and lost. \n\nThey will still exist in a hidden data volume, which can be recovered using standard docker techniques, but that is much more complex than just starting with a named volume as described above.",
        "x": 350,
        "y": 80,
        "wires": []
    },
    {
        "id": "2f32658451e5e26a",
        "type": "comment",
        "z": "564e011e075fac28",
        "name": "ESP8266 MQTT Temperature Thermistor NTC ",
        "info": "",
        "x": 190,
        "y": 180,
        "wires": []
    },
    {
        "id": "596b024d4a2187bf",
        "type": "mqtt in",
        "z": "564e011e075fac28",
        "name": "",
        "topic": "sensor/NTC/tempInC",
        "qos": "2",
        "datatype": "auto-detect",
        "broker": "8234be649768a71d",
        "nl": false,
        "rap": false,
        "inputs": 0,
        "x": 140,
        "y": 240,
        "wires": [
            [
                "70ad455aa3131199",
                "4475b4bb4a421d76",
                "4a4eca621173be83"
            ]
        ]
    },
    {
        "id": "7ee41d995ab826ad",
        "type": "comment",
        "z": "564e011e075fac28",
        "name": "ESP8266 MQTT MQ135",
        "info": "",
        "x": 130,
        "y": 300,
        "wires": []
    },
    {
        "id": "91372448333e6e0a",
        "type": "mqtt in",
        "z": "564e011e075fac28",
        "name": "",
        "topic": "sensor/MQ135/ammonia",
        "qos": "2",
        "datatype": "auto-detect",
        "broker": "8234be649768a71d",
        "nl": false,
        "rap": false,
        "inputs": 0,
        "x": 130,
        "y": 360,
        "wires": [
            [
                "ef9378b8d47e25a2",
                "743f810ef6189b68",
                "4a4eca621173be83"
            ]
        ]
    },
    {
        "id": "481c6f74cdf6a946",
        "type": "comment",
        "z": "564e011e075fac28",
        "name": "ESP8266 MQTT Ph",
        "info": "",
        "x": 110,
        "y": 420,
        "wires": []
    },
    {
        "id": "4e4d59c98576347d",
        "type": "mqtt in",
        "z": "564e011e075fac28",
        "name": "",
        "topic": "sensor/PH/phValue",
        "qos": "2",
        "datatype": "auto-detect",
        "broker": "8234be649768a71d",
        "nl": false,
        "rap": false,
        "inputs": 0,
        "x": 150,
        "y": 480,
        "wires": [
            [
                "f454422b23522aef",
                "084f54d093f14b96",
                "4a4eca621173be83"
            ]
        ]
    },
    {
        "id": "274cf9e79cee4818",
        "type": "debug",
        "z": "564e011e075fac28",
        "name": "debug",
        "active": true,
        "tosidebar": true,
        "console": false,
        "tostatus": false,
        "complete": "topic",
        "targetType": "msg",
        "statusVal": "",
        "statusType": "auto",
        "x": 1070,
        "y": 360,
        "wires": []
    },
    {
        "id": "379237cafb075281",
        "type": "function",
        "z": "564e011e075fac28",
        "name": "sending",
        "func": "// Log the values before constructing the SQL query\nconsole.log(\"Temperature_NTC:\", msg.payload[1]);\nconsole.log(\"Ammonia_MQ135:\", msg.payload[2]);\nconsole.log(\"Ph_Sensor:\", msg.payload[0]);\n\n// Your existing code to construct the SQL query\nmsg.topic = \"INSERT INTO pale_db.pale_tables (Temperature_NTC, Ammonia_MQ135, Ph_Sensor)\" +\n            \"VALUES ('\" + msg.payload[0] + \"','\" + msg.payload[1] + \"','\" + msg.payload[2] + \"')\";\n\n// Log the constructed SQL query\nconsole.log(\"Constructed SQL query:\", msg.topic);\n\n// Send the message to the MySQL node\nreturn msg;\n\n// // Construct the SQL query\n// msg.topic = \"INSERT INTO pale_db.pale_tables (Temperature_NTC, Ammonia_MQ135, Ph_Sensor)\" +\n//             \"VALUES (\" + parseFloat(msg.payload[0]) + \",\" + parseFloat(msg.payload[1]) + \",\" + parseFloat(msg.payload[2]) +\")\";\n\n// // Log the constructed SQL query\n// console.log(\"Constructed SQL query:\", msg.topic);\n\n// return msg;\n\n// // Convert string values with comma to float\n// const temperatureNTC = parseFloat(msg.payload[0].replace(',', '.'));\n// const ammoniaMQ135 = parseFloat(msg.payload[1].replace(',', '.'));\n// const phSensor = parseFloat(msg.payload[2].replace(',', '.'));\n\n// // Construct the SQL query\n// msg.topic = \"INSERT INTO pale_db.pale_tables (Temperature_NTC, Ammonia_MQ135, Ph_Sensor)\" +\n//             \"VALUES (\" + temperatureNTC + \",\" + ammoniaMQ135 + \",\" + phSensor +\")\";\n\n// // Log the constructed SQL query\n// console.log(\"Constructed SQL query:\", msg.topic);\n\n// return msg;\n\n// // Convert string values with comma to float\n// const temperatureNTC = parseFloat(msg.payload[0].replace(',', '.'));\n// const ammoniaMQ135 = parseFloat(msg.payload[1].replace(',', '.'));\n// const phSensor = parseFloat(msg.payload[2].replace(',', '.'));\n\n// // Construct the SQL query\n// msg.topic = \"INSERT INTO pale_db.pale_tables (Temperature_NTC, Ammonia_MQ135, Ph_Sensor)\" +\n//             \"VALUES (\" + temperatureNTC + \",\" + ammoniaMQ135 + \",\" + phSensor +\")\";\n\n// // Log the constructed SQL query\n// console.log(\"Constructed SQL query:\", msg.topic);\n\n// return msg;\n",
        "outputs": 1,
        "timeout": 0,
        "noerr": 0,
        "initialize": "",
        "finalize": "",
        "libs": [],
        "x": 700,
        "y": 360,
        "wires": [
            [
                "7b7b89dbc3d77531"
            ]
        ]
    },
    {
        "id": "4a4eca621173be83",
        "type": "join",
        "z": "564e011e075fac28",
        "name": "",
        "mode": "custom",
        "build": "array",
        "property": "payload",
        "propertyType": "msg",
        "key": "topic",
        "joiner": "\\n",
        "joinerType": "str",
        "accumulate": false,
        "timeout": "",
        "count": "3",
        "reduceRight": false,
        "reduceExp": "",
        "reduceInit": "",
        "reduceInitType": "num",
        "reduceFixup": "",
        "x": 550,
        "y": 360,
        "wires": [
            [
                "379237cafb075281"
            ]
        ]
    },
    {
        "id": "e83df2ddadea771c",
        "type": "comment",
        "z": "564e011e075fac28",
        "name": "ESP8266 MQTT Alert & Relay for Katup",
        "info": "",
        "x": 170,
        "y": 560,
        "wires": []
    },
    {
        "id": "eb7ce95e50a684fa",
        "type": "mqtt out",
        "z": "564e011e075fac28",
        "name": "",
        "topic": "katup",
        "qos": "",
        "retain": "",
        "respTopic": "",
        "contentType": "",
        "userProps": "",
        "correl": "",
        "expiry": "",
        "broker": "8234be649768a71d",
        "x": 350,
        "y": 600,
        "wires": []
    },
    {
        "id": "cf3a5954b7521194",
        "type": "debug",
        "z": "564e011e075fac28",
        "name": "debug",
        "active": true,
        "tosidebar": true,
        "console": false,
        "tostatus": false,
        "complete": "payload",
        "targetType": "msg",
        "statusVal": "",
        "statusType": "auto",
        "x": 350,
        "y": 680,
        "wires": []
    },
    {
        "id": "e36c8b21a6108e93",
        "type": "ui_switch",
        "z": "564e011e075fac28",
        "name": "Katup",
        "label": "Switch Katup",
        "tooltip": "",
        "group": "071e31b8c3ba162e",
        "order": 0,
        "width": 0,
        "height": 0,
        "passthru": true,
        "decouple": "false",
        "topic": "katup",
        "topicType": "str",
        "style": "",
        "onvalue": "on",
        "onvalueType": "str",
        "onicon": "",
        "oncolor": "",
        "offvalue": "off",
        "offvalueType": "str",
        "officon": "",
        "offcolor": "",
        "animate": false,
        "className": "",
        "x": 190,
        "y": 640,
        "wires": [
            [
                "eb7ce95e50a684fa",
                "cf3a5954b7521194"
            ]
        ]
    },
    {
        "id": "70ad455aa3131199",
        "type": "ui_gauge",
        "z": "564e011e075fac28",
        "name": "",
        "group": "bd16d2bb7a66f39a",
        "order": 2,
        "width": 0,
        "height": 0,
        "gtype": "gage",
        "title": "Temperature In C",
        "label": "ºC",
        "format": "{{value}}",
        "min": "0",
        "max": "100",
        "colors": [
            "#00b500",
            "#e6e600",
            "#ca3838"
        ],
        "seg1": "",
        "seg2": "",
        "diff": false,
        "className": "",
        "x": 390,
        "y": 220,
        "wires": []
    },
    {
        "id": "ef9378b8d47e25a2",
        "type": "ui_gauge",
        "z": "564e011e075fac28",
        "name": "",
        "group": "c079f1c984b05fe4",
        "order": 2,
        "width": 0,
        "height": 0,
        "gtype": "gage",
        "title": "Ammonia",
        "label": "mg/L",
        "format": "{{value}}",
        "min": "0",
        "max": "2",
        "colors": [
            "#00b500",
            "#e6e600",
            "#ca3838"
        ],
        "seg1": "",
        "seg2": "",
        "diff": false,
        "className": "",
        "x": 360,
        "y": 340,
        "wires": []
    },
    {
        "id": "f454422b23522aef",
        "type": "ui_gauge",
        "z": "564e011e075fac28",
        "name": "",
        "group": "7425084c949fae29",
        "order": 2,
        "width": 0,
        "height": 0,
        "gtype": "gage",
        "title": "Sensor Ph",
        "label": "pH",
        "format": "{{value}}",
        "min": "0",
        "max": "15",
        "colors": [
            "#00b500",
            "#e6e600",
            "#ca3838"
        ],
        "seg1": "",
        "seg2": "",
        "diff": false,
        "className": "",
        "x": 370,
        "y": 460,
        "wires": []
    },
    {
        "id": "4475b4bb4a421d76",
        "type": "ui_chart",
        "z": "564e011e075fac28",
        "name": "",
        "group": "bd16d2bb7a66f39a",
        "order": 3,
        "width": 0,
        "height": 0,
        "label": "Water Temp",
        "chartType": "line",
        "legend": "false",
        "xformat": "HH:mm:ss",
        "interpolate": "linear",
        "nodata": "",
        "dot": false,
        "ymin": "0",
        "ymax": "50",
        "removeOlder": 1,
        "removeOlderPoints": "",
        "removeOlderUnit": "3600",
        "cutout": "",
        "useOneColor": false,
        "useUTC": false,
        "colors": [
            "#1f77b4",
            "#aec7e8",
            "#ff7f0e",
            "#2ca02c",
            "#98df8a",
            "#d62728",
            "#ff9896",
            "#9467bd",
            "#c5b0d5"
        ],
        "outputs": 1,
        "useDifferentColor": false,
        "className": "",
        "x": 370,
        "y": 260,
        "wires": [
            []
        ]
    },
    {
        "id": "743f810ef6189b68",
        "type": "ui_chart",
        "z": "564e011e075fac28",
        "name": "",
        "group": "c079f1c984b05fe4",
        "order": 4,
        "width": 0,
        "height": 0,
        "label": "Ammonia",
        "chartType": "line",
        "legend": "false",
        "xformat": "HH:mm:ss",
        "interpolate": "linear",
        "nodata": "",
        "dot": false,
        "ymin": "0",
        "ymax": "2",
        "removeOlder": 1,
        "removeOlderPoints": "",
        "removeOlderUnit": "3600",
        "cutout": 0,
        "useOneColor": false,
        "useUTC": false,
        "colors": [
            "#1f77b4",
            "#aec7e8",
            "#ff7f0e",
            "#2ca02c",
            "#98df8a",
            "#d62728",
            "#ff9896",
            "#9467bd",
            "#c5b0d5"
        ],
        "outputs": 1,
        "useDifferentColor": false,
        "className": "",
        "x": 360,
        "y": 380,
        "wires": [
            []
        ]
    },
    {
        "id": "084f54d093f14b96",
        "type": "ui_chart",
        "z": "564e011e075fac28",
        "name": "",
        "group": "7425084c949fae29",
        "order": 4,
        "width": 0,
        "height": 0,
        "label": "Sensor Ph",
        "chartType": "line",
        "legend": "false",
        "xformat": "HH:mm:ss",
        "interpolate": "linear",
        "nodata": "",
        "dot": false,
        "ymin": "0",
        "ymax": "15",
        "removeOlder": 1,
        "removeOlderPoints": "",
        "removeOlderUnit": "3600",
        "cutout": 0,
        "useOneColor": false,
        "useUTC": false,
        "colors": [
            "#1f77b4",
            "#aec7e8",
            "#ff7f0e",
            "#2ca02c",
            "#98df8a",
            "#d62728",
            "#ff9896",
            "#9467bd",
            "#c5b0d5"
        ],
        "outputs": 1,
        "useDifferentColor": false,
        "className": "",
        "x": 370,
        "y": 500,
        "wires": [
            []
        ]
    },
    {
        "id": "904a1b1b8cc360db",
        "type": "link in",
        "z": "564e011e075fac28",
        "name": "link in 1",
        "links": [],
        "x": 95,
        "y": 640,
        "wires": [
            [
                "e36c8b21a6108e93"
            ]
        ]
    },
    {
        "id": "7b7b89dbc3d77531",
        "type": "mysql",
        "z": "564e011e075fac28",
        "mydb": "372add3cda52af51",
        "name": "",
        "x": 890,
        "y": 360,
        "wires": [
            [
                "274cf9e79cee4818"
            ]
        ]
    },
    {
        "id": "98c7873797d820ac",
        "type": "comment",
        "z": "3572d07acf83b089",
        "name": "WARNING: please check you have started this container with a volume that is mounted to /data\\n otherwise any flow changes are lost when you redeploy or upgrade the container\\n (e.g. upgrade to a more recent node-red docker image).\\n  If you are using named volumes you can ignore this warning.\\n Double click or see info side panel to learn how to start Node-RED in Docker to save your work",
        "info": "\nTo start docker with a bind mount volume (-v option), for example:\n\n```\ndocker run -it -p 1880:1880 -v /home/user/node_red_data:/data --name mynodered nodered/node-red\n```\n\nwhere `/home/user/node_red_data` is a directory on your host machine where you want to store your flows.\n\nIf you do not do this then you can experiment and redploy flows, but if you restart or upgrade the container the flows will be disconnected and lost. \n\nThey will still exist in a hidden data volume, which can be recovered using standard docker techniques, but that is much more complex than just starting with a named volume as described above.",
        "x": 350,
        "y": 80,
        "wires": []
    },
    {
        "id": "6e8fa6f8869fc3b7",
        "type": "comment",
        "z": "3572d07acf83b089",
        "name": "ESP8266 MQTT Temperature Thermistor NTC ",
        "info": "",
        "x": 190,
        "y": 180,
        "wires": []
    },
    {
        "id": "41674a0a26b1ac4d",
        "type": "mqtt in",
        "z": "3572d07acf83b089",
        "name": "",
        "topic": "sensor/NTC/tempInC",
        "qos": "2",
        "datatype": "auto-detect",
        "broker": "8234be649768a71d",
        "nl": false,
        "rap": false,
        "inputs": 0,
        "x": 140,
        "y": 240,
        "wires": [
            [
                "a7f6517c393283b2",
                "6b57b684ca2c8103",
                "e5bc7c52c347ab10"
            ]
        ]
    },
    {
        "id": "0d2b82f6dd1ad8d8",
        "type": "comment",
        "z": "3572d07acf83b089",
        "name": "ESP8266 MQTT MQ135",
        "info": "",
        "x": 130,
        "y": 300,
        "wires": []
    },
    {
        "id": "1c8bd2864d2470b2",
        "type": "mqtt in",
        "z": "3572d07acf83b089",
        "name": "",
        "topic": "sensor/MQ135/ammonia",
        "qos": "2",
        "datatype": "auto-detect",
        "broker": "8234be649768a71d",
        "nl": false,
        "rap": false,
        "inputs": 0,
        "x": 130,
        "y": 360,
        "wires": [
            [
                "8a8ab33f49d5a26e",
                "cb07d95838933727",
                "e5bc7c52c347ab10"
            ]
        ]
    },
    {
        "id": "6c0b567b3c1cb8ea",
        "type": "comment",
        "z": "3572d07acf83b089",
        "name": "ESP8266 MQTT Ph",
        "info": "",
        "x": 110,
        "y": 420,
        "wires": []
    },
    {
        "id": "df731195c77c1b0c",
        "type": "mqtt in",
        "z": "3572d07acf83b089",
        "name": "",
        "topic": "sensor/PH/phValue",
        "qos": "2",
        "datatype": "auto-detect",
        "broker": "8234be649768a71d",
        "nl": false,
        "rap": false,
        "inputs": 0,
        "x": 150,
        "y": 480,
        "wires": [
            [
                "9135cb13f14ad8a8",
                "a2b9cd59b12e2f9f",
                "e5bc7c52c347ab10"
            ]
        ]
    },
    {
        "id": "5ba9a02db5507b84",
        "type": "debug",
        "z": "3572d07acf83b089",
        "name": "debug 6",
        "active": true,
        "tosidebar": true,
        "console": false,
        "tostatus": false,
        "complete": "topic",
        "targetType": "msg",
        "statusVal": "",
        "statusType": "auto",
        "x": 1080,
        "y": 360,
        "wires": []
    },
    {
        "id": "36c31756d3a4d053",
        "type": "function",
        "z": "3572d07acf83b089",
        "name": "sending",
        "func": "// Log the values before constructing the SQL query\nconsole.log(\"Temperature_NTC:\", msg.payload[0]);\nconsole.log(\"Ammonia_MQ135:\", msg.payload[1]);\nconsole.log(\"Ph_Sensor:\", msg.payload[2]);\n\n// Your existing code to construct the SQL query\nmsg.topic = \"INSERT INTO pale_db.pale_tables (Temperature_NTC, Ammonia_MQ135, Ph_Sensor)\" +\n            \"VALUES ('\" + msg.payload[0] + \"','\" + msg.payload[1] + \"','\" + msg.payload[2] + \"')\";\n\n// Log the constructed SQL query\nconsole.log(\"Constructed SQL query:\", msg.topic);\n\n// Send the message to the MySQL node\nreturn msg;\n\n// // Construct the SQL query\n// msg.topic = \"INSERT INTO pale_db.pale_tables (Temperature_NTC, Ammonia_MQ135, Ph_Sensor)\" +\n//             \"VALUES (\" + parseFloat(msg.payload[0]) + \",\" + parseFloat(msg.payload[1]) + \",\" + parseFloat(msg.payload[2]) +\")\";\n\n// // Log the constructed SQL query\n// console.log(\"Constructed SQL query:\", msg.topic);\n\n// return msg;\n\n// // Convert string values with comma to float\n// const temperatureNTC = parseFloat(msg.payload[0].replace(',', '.'));\n// const ammoniaMQ135 = parseFloat(msg.payload[1].replace(',', '.'));\n// const phSensor = parseFloat(msg.payload[2].replace(',', '.'));\n\n// // Construct the SQL query\n// msg.topic = \"INSERT INTO pale_db.pale_tables (Temperature_NTC, Ammonia_MQ135, Ph_Sensor)\" +\n//             \"VALUES (\" + temperatureNTC + \",\" + ammoniaMQ135 + \",\" + phSensor +\")\";\n\n// // Log the constructed SQL query\n// console.log(\"Constructed SQL query:\", msg.topic);\n\n// return msg;\n\n// // Convert string values with comma to float\n// const temperatureNTC = parseFloat(msg.payload[0].replace(',', '.'));\n// const ammoniaMQ135 = parseFloat(msg.payload[1].replace(',', '.'));\n// const phSensor = parseFloat(msg.payload[2].replace(',', '.'));\n\n// // Construct the SQL query\n// msg.topic = \"INSERT INTO pale_db.pale_tables (Temperature_NTC, Ammonia_MQ135, Ph_Sensor)\" +\n//             \"VALUES (\" + temperatureNTC + \",\" + ammoniaMQ135 + \",\" + phSensor +\")\";\n\n// // Log the constructed SQL query\n// console.log(\"Constructed SQL query:\", msg.topic);\n\n// return msg;\n",
        "outputs": 1,
        "timeout": 0,
        "noerr": 0,
        "initialize": "",
        "finalize": "",
        "libs": [],
        "x": 700,
        "y": 360,
        "wires": [
            [
                "879de74e815113fb"
            ]
        ]
    },
    {
        "id": "e5bc7c52c347ab10",
        "type": "join",
        "z": "3572d07acf83b089",
        "name": "",
        "mode": "custom",
        "build": "array",
        "property": "payload",
        "propertyType": "msg",
        "key": "topic",
        "joiner": "\\n",
        "joinerType": "str",
        "accumulate": false,
        "timeout": "",
        "count": "3",
        "reduceRight": false,
        "reduceExp": "",
        "reduceInit": "",
        "reduceInitType": "num",
        "reduceFixup": "",
        "x": 550,
        "y": 360,
        "wires": [
            [
                "36c31756d3a4d053"
            ]
        ]
    },
    {
        "id": "5102ce7d4df28caf",
        "type": "comment",
        "z": "3572d07acf83b089",
        "name": "ESP8266 MQTT Alert & Relay for Katup",
        "info": "",
        "x": 170,
        "y": 560,
        "wires": []
    },
    {
        "id": "3c59cd5639a5a2e4",
        "type": "mqtt out",
        "z": "3572d07acf83b089",
        "name": "",
        "topic": "katup",
        "qos": "",
        "retain": "",
        "respTopic": "",
        "contentType": "",
        "userProps": "",
        "correl": "",
        "expiry": "",
        "broker": "8234be649768a71d",
        "x": 350,
        "y": 600,
        "wires": []
    },
    {
        "id": "9b71f449cc485fd1",
        "type": "debug",
        "z": "3572d07acf83b089",
        "name": "debug 7",
        "active": true,
        "tosidebar": true,
        "console": false,
        "tostatus": false,
        "complete": "false",
        "statusVal": "",
        "statusType": "auto",
        "x": 360,
        "y": 680,
        "wires": []
    },
    {
        "id": "841f109f37dd53f6",
        "type": "ui_switch",
        "z": "3572d07acf83b089",
        "name": "Katup",
        "label": "Switch Katup",
        "tooltip": "",
        "group": "071e31b8c3ba162e",
        "order": 0,
        "width": 0,
        "height": 0,
        "passthru": true,
        "decouple": "false",
        "topic": "katup",
        "topicType": "str",
        "style": "",
        "onvalue": "on",
        "onvalueType": "str",
        "onicon": "",
        "oncolor": "",
        "offvalue": "off",
        "offvalueType": "str",
        "officon": "",
        "offcolor": "",
        "animate": false,
        "className": "",
        "x": 190,
        "y": 640,
        "wires": [
            [
                "3c59cd5639a5a2e4",
                "9b71f449cc485fd1"
            ]
        ]
    },
    {
        "id": "a7f6517c393283b2",
        "type": "ui_gauge",
        "z": "3572d07acf83b089",
        "name": "",
        "group": "bd16d2bb7a66f39a",
        "order": 2,
        "width": 0,
        "height": 0,
        "gtype": "gage",
        "title": "Temperature In C",
        "label": "ºC",
        "format": "{{value}}",
        "min": "0",
        "max": "100",
        "colors": [
            "#00b500",
            "#e6e600",
            "#ca3838"
        ],
        "seg1": "",
        "seg2": "",
        "diff": false,
        "className": "",
        "x": 390,
        "y": 220,
        "wires": []
    },
    {
        "id": "8a8ab33f49d5a26e",
        "type": "ui_gauge",
        "z": "3572d07acf83b089",
        "name": "",
        "group": "c079f1c984b05fe4",
        "order": 2,
        "width": 0,
        "height": 0,
        "gtype": "gage",
        "title": "Ammonia",
        "label": "mg/L",
        "format": "{{value}}",
        "min": "0",
        "max": "5",
        "colors": [
            "#00b500",
            "#e6e600",
            "#ca3838"
        ],
        "seg1": "",
        "seg2": "",
        "diff": false,
        "className": "",
        "x": 360,
        "y": 340,
        "wires": []
    },
    {
        "id": "9135cb13f14ad8a8",
        "type": "ui_gauge",
        "z": "3572d07acf83b089",
        "name": "",
        "group": "7425084c949fae29",
        "order": 2,
        "width": 0,
        "height": 0,
        "gtype": "gage",
        "title": "Sensor Ph",
        "label": "pH",
        "format": "{{value}}",
        "min": "0",
        "max": "50",
        "colors": [
            "#00b500",
            "#e6e600",
            "#ca3838"
        ],
        "seg1": "",
        "seg2": "",
        "diff": false,
        "className": "",
        "x": 370,
        "y": 460,
        "wires": []
    },
    {
        "id": "6b57b684ca2c8103",
        "type": "ui_chart",
        "z": "3572d07acf83b089",
        "name": "",
        "group": "bd16d2bb7a66f39a",
        "order": 3,
        "width": 0,
        "height": 0,
        "label": "Water Temp",
        "chartType": "line",
        "legend": "false",
        "xformat": "HH:mm:ss",
        "interpolate": "linear",
        "nodata": "",
        "dot": false,
        "ymin": "0",
        "ymax": "50",
        "removeOlder": 1,
        "removeOlderPoints": "",
        "removeOlderUnit": "3600",
        "cutout": "",
        "useOneColor": false,
        "useUTC": false,
        "colors": [
            "#1f77b4",
            "#aec7e8",
            "#ff7f0e",
            "#2ca02c",
            "#98df8a",
            "#d62728",
            "#ff9896",
            "#9467bd",
            "#c5b0d5"
        ],
        "outputs": 1,
        "useDifferentColor": false,
        "className": "",
        "x": 370,
        "y": 260,
        "wires": [
            []
        ]
    },
    {
        "id": "cb07d95838933727",
        "type": "ui_chart",
        "z": "3572d07acf83b089",
        "name": "",
        "group": "c079f1c984b05fe4",
        "order": 4,
        "width": 0,
        "height": 0,
        "label": "Ammonia",
        "chartType": "line",
        "legend": "false",
        "xformat": "HH:mm:ss",
        "interpolate": "linear",
        "nodata": "",
        "dot": false,
        "ymin": "0",
        "ymax": "5",
        "removeOlder": 1,
        "removeOlderPoints": "",
        "removeOlderUnit": "3600",
        "cutout": 0,
        "useOneColor": false,
        "useUTC": false,
        "colors": [
            "#1f77b4",
            "#aec7e8",
            "#ff7f0e",
            "#2ca02c",
            "#98df8a",
            "#d62728",
            "#ff9896",
            "#9467bd",
            "#c5b0d5"
        ],
        "outputs": 1,
        "useDifferentColor": false,
        "className": "",
        "x": 360,
        "y": 380,
        "wires": [
            []
        ]
    },
    {
        "id": "a2b9cd59b12e2f9f",
        "type": "ui_chart",
        "z": "3572d07acf83b089",
        "name": "",
        "group": "7425084c949fae29",
        "order": 4,
        "width": 0,
        "height": 0,
        "label": "Sensor Ph",
        "chartType": "line",
        "legend": "false",
        "xformat": "HH:mm:ss",
        "interpolate": "linear",
        "nodata": "",
        "dot": false,
        "ymin": "0",
        "ymax": "50",
        "removeOlder": 1,
        "removeOlderPoints": "",
        "removeOlderUnit": "3600",
        "cutout": 0,
        "useOneColor": false,
        "useUTC": false,
        "colors": [
            "#1f77b4",
            "#aec7e8",
            "#ff7f0e",
            "#2ca02c",
            "#98df8a",
            "#d62728",
            "#ff9896",
            "#9467bd",
            "#c5b0d5"
        ],
        "outputs": 1,
        "useDifferentColor": false,
        "className": "",
        "x": 370,
        "y": 500,
        "wires": [
            []
        ]
    },
    {
        "id": "4aefff98f5f43b5b",
        "type": "link in",
        "z": "3572d07acf83b089",
        "name": "link in 2",
        "links": [],
        "x": 185,
        "y": 640,
        "wires": [
            [
                "841f109f37dd53f6"
            ]
        ]
    },
    {
        "id": "879de74e815113fb",
        "type": "mysql",
        "z": "3572d07acf83b089",
        "mydb": "372add3cda52af51",
        "name": "",
        "x": 890,
        "y": 360,
        "wires": [
            [
                "5ba9a02db5507b84"
            ]
        ]
    }
]
